// Logisim project Cau1.circ as structural Verilog: 1 circuit, main circuit main
module main (
  input  in_1,
  input  in_2,
  input  in_3,
  input  in_4,
  input  in_5,
  input  in_6,
  input  in_7,
  input  in_8,
  input  in_9,
  input  in_10,
  input  in_11,
  input  in_12,
  input  [7:0] in_13,
  input  in_14,
  input  in_15,
  input  in_16,
  output out_17,
  output out_18,
  output out_19,
  output out_20,
  output out_21,
  output out_22,
  output out_23,
  output out_24,
  output out_25,
  output out_26,
  output [7:0] out_27,
  output out_28
);

  wire clock_1_out, clock_2_out, clock_3_out;

  and and_1 (out_17, in_1, in_2);
  or or_1 (out_18, in_3, in_4);
  not not_1 (out_21, in_6);
  xor xor_1 (out_22, in_7, in_8);
  xnor xnor_1 (out_25, in_10, in_11);
  nand nand_1 (out_26, in_12, in_14);
  nor nor_1 (out_28, in_15, in_16);
  Clock clock_1 (.out(clock_1_out));
  Clock clock_2 (.out(clock_2_out));
  D_Flip_Flop #(.trigger("high")) d_ff_1 (
    .clk(clock_1_out), .D(in_5), .Q(out_19), .Qn(out_20));  // open: preset, en, reset
  D_Flip_Flop #(.trigger("falling")) d_ff_2 (
    .clk(clock_2_out), .D(in_9), .Q(out_23), .Qn(out_24));  // open: preset, en, reset
  Clock clock_3 (.out(clock_3_out));
  Register register_1 (.D(in_13), .Q(out_27), .clk(clock_3_out));  // open: en, clr

  // Notes on the sheet:
  //   AND
  //   OR
  //   NOT
  //   XOR
  //   XNOR
  //   NAND
  //   NOR
  //   D-latch
  //   D-flip-flop
  //   Register
endmodule
