// Logisim project Cau2.circ as structural Verilog: 1 circuit, main circuit main
module main (
  input  A,
  input  B,
  input  C,
  input  D,
  output A_o,
  output B_o,
  output C_o,
  output D_o
);

  wire clock_1_out;

  Clock clock_1 (.out(clock_1_out));
  Register #(.width(4)) register_1 (
    .D({D, C, B, A}), .en(1'b1), .Q({D_o, C_o, B_o, A_o}), .clk(clock_1_out));  // open: clr

  // Notes on the sheet:
  //   clock
endmodule
