// Logisim project bai2.1.circ as structural Verilog: 2 circuits, main circuit ALU
module ALU (
  input  [7:0] A,
  input  [7:0] B,
  input  [1:0] in_3,
  output [7:0] out_4
);

  wire [7:0] adder_1_out, AND_out, NAND_out, subtractor_1_out;

  Adder adder_1 (.a(A), .b(B), .out(adder_1_out));  // open: cin, cout
  Subtractor subtractor_1 (.a(A), .b(B), .out(subtractor_1_out));  // open: bin, bout
  assign AND_out = A & B;  // AND_Gate AND, 8 bits wide
  assign NAND_out = ~(A & B);  // NAND_Gate NAND, 8 bits wide
  Multiplexer #(.select(2), .width(8)) multiplexer_1 (
    .in0(adder_1_out), .in1(subtractor_1_out), .in2(AND_out), .in3(NAND_out), .out(out_4), .sel(in_3));  // open: en
endmodule

module ALU_enhanced (
  input  [7:0] in_1,
  input  [7:0] in_2,
  input  [2:0] in_3,
  output [7:0] out_4
);

  wire [7:0] adder_1_out, adder_2_out, AND_out, NOT_out, OR_out, subtractor_1_out, subtractor_2_out, XOR_out;

  Adder adder_1 (.a(in_1), .b(in_2), .out(adder_1_out));  // open: cin, cout
  Adder adder_2 (.a(in_1), .b(8'h1), .out(adder_2_out));  // open: cin, cout
  Subtractor subtractor_1 (.a(in_1), .b(in_2), .out(subtractor_1_out));  // open: bin, bout
  Subtractor subtractor_2 (.a(in_1), .b(8'h1), .out(subtractor_2_out));  // open: bin, bout
  assign AND_out = in_1 & in_2;  // AND_Gate AND, 8 bits wide
  assign OR_out = in_1 | in_2;  // OR_Gate OR, 8 bits wide
  assign NOT_out = ~in_1;  // NOT_Gate NOT, 8 bits wide
  assign XOR_out = in_1 ^ in_2;  // XOR_Gate XOR, 8 bits wide
  Multiplexer #(.select(3), .width(8)) multiplexer_1 (
    .in0(adder_1_out), .in1(adder_2_out), .in2(subtractor_1_out), .in3(subtractor_2_out), .in4(AND_out),
    .in5(OR_out), .in6(NOT_out), .in7(XOR_out), .out(out_4), .sel(in_3));  // open: en
endmodule
