// Logisim project bai3.circ as structural Verilog: 3 circuits, main circuit main
module main (
  input  A,
  input  B,
  input  C,
  output out_4
);

  wire and_1_out, and_2_out, not_1_out, not_2_out, not_3_out;

  not not_1 (not_1_out, A);
  not not_2 (not_2_out, C);
  not not_3 (not_3_out, B);
  and and_1 (and_1_out, not_1_out, B, not_2_out);
  and and_2 (and_2_out, A, not_3_out, C);
  or or_1 (out_4, and_1_out, and_2_out);
endmodule

module sub1 (
  input  A,
  input  B,
  input  C,
  output out_4
);

  wire and_1_out, and_2_out, and_3_out, and_4_out, not_1_out, not_2_out, not_3_out;

  not not_1 (not_1_out, A);
  not not_2 (not_2_out, B);
  not not_3 (not_3_out, C);
  and and_1 (and_1_out, not_1_out, not_2_out, not_3_out);
  and and_2 (and_2_out, not_1_out, B, C);
  and and_3 (and_3_out, A, B, not_3_out);
  and and_4 (and_4_out, A, not_2_out, C);
  or or_1 (out_4, and_1_out, and_2_out, and_3_out, and_4_out);
endmodule

module complete (
  input  A,
  input  B,
  input  C,
  output out_4,
  output out_5,
  output out_6
);

  main main_1 (.A(A), .B(B), .C(C), .out_4(out_4));
  sub1 sub1_1 (.A(A), .B(B), .C(C), .out_4(out_5));
  main main_2 (.A(A), .B(B), .C(C), .out_4(out_6));
endmodule
